# Fritzing sketch fritizng_sketch (saved by Fritzing 0.9.3b)
breadboards: 1

parts:
  Part1 = Arduino Pro Mini v13
  IC1 = Voltage Regulator [part_number="LF8L33 3.3V" package=to-92]
  C3 = Ceramic Capacitor [capacitance=0.33µF package="100 mil [THT, multilayer]"]
  C4 = Ceramic Capacitor [capacitance=100nF package="100 mil [THT, multilayer]"]
  IC2 = '4050 Hex Buffer
  Nokia_5110_LCD_Module1 = Nokia 5110 LCD basado en PCD8544
  Part2 = MicroSD Card Module
  S1 = Pushbutton [package="[THT]"]
  S2 = Pushbutton [package="[THT]"]
  S3 = Pushbutton [package="[THT]"]
  S4 = Pushbutton [package="[THT]"]
  R1 = Resistor [tolerance=±5% resistance=1k package=THT]
  R2 = Resistor [tolerance=±5% resistance=100k package=THT]
  R3 = Resistor [tolerance=±5% resistance=22k package=THT]
  R4 = Resistor [tolerance=±5% resistance=41k package=THT]
  R5 = Resistor [tolerance=±5% resistance=51k package=THT]

nets (from the schematic view):
  VCC: Part1.VCC, IC1.OUT, C3.1, Part2.VCC, R1.Pin_0, R3.Pin_0, R4.Pin_0, R5.Pin_0
  GND: Part1.GND, IC1.IN, C3.0, C4.0, IC2.VSS, Nokia_5110_LCD_Module1.GND, Part2.GND, R2.Pin_0
  N1: Part1.A3, S1.Pin_3, S1.Pin_4, S2.Pin_3, S2.Pin_4, S3.Pin_3, S3.Pin_4, S4.Pin_3, S4.Pin_4, R2.Pin_1
  N2: Part1.D13/SCK, IC2.A, Part2.SCK
  N3: Part1.D12/MISO, Part2.MISO
  N4: Part1.D11_PWM/MOSI, IC2.B, Part2.MOSI
  N5: Part1.D10_PWM/SS, Part2.CS
  N6: Part1.D5_PWM, IC2.C
  N7: Part1.D4, IC2.F
  N8: Part1.D3_PWM, IC2.E
  N9: Part1.D2, IC2.D
  N10: IC2.G, Nokia_5110_LCD_Module1.CLK
  N11: IC2.H, Nokia_5110_LCD_Module1.DIN
  N12: IC2.I, Nokia_5110_LCD_Module1.LIGHT
  N13: IC2.J, Nokia_5110_LCD_Module1.RST
  N14: IC2.K, Nokia_5110_LCD_Module1.CE
  N15: IC2.L, Nokia_5110_LCD_Module1.DC
  N16: S1.Pin_1, S1.Pin_2, R1.Pin_1
  N17: S2.Pin_1, S2.Pin_2, R3.Pin_1
  N18: S3.Pin_1, S3.Pin_2, R4.Pin_1
  N19: S4.Pin_1, S4.Pin_2, R5.Pin_1

custom parts:
  Nokia 5110 LCD basado en PCD8544: Módulo Nokia 5110 LCD basado en el controlador PCD8544. Versión de 8 pines (sólo entrada).
